// Digital circuit 256B_MEM.dig as structural Verilog
module _256B_MEM (
  input  [7:0] A,
  input  [7:0] WD,
  input  WE,
  input  CLK,
  output [7:0] RD
);

  wire and_1_out, and_2_out, and_3_out, and_4_out, and_5_out, and_6_out, and_7_out, and_8_out;
  wire [7:0] _64b_mem_1_rd, _64b_mem_2_rd, _64b_mem_3_rd, _64b_mem_4_rd;

  and and_1 (and_1_out, A[0], A[1]);
  and and_2 (and_2_out, ~A[0], A[1]);  // And
  and and_3 (and_3_out, A[0], ~A[1]);  // And
  and and_4 (and_4_out, ~A[0], ~A[1]);  // And
  and and_5 (and_5_out, and_1_out, WE);
  and and_6 (and_6_out, and_2_out, WE);
  and and_7 (and_7_out, and_3_out, WE);
  and and_8 (and_8_out, and_4_out, WE);
  _64B_MEM _64b_mem_1 (.A(A[7:2]), .WD(WD), .WE(and_5_out), .CLK(CLK), .RD(_64b_mem_1_rd));
  _64B_MEM _64b_mem_2 (.A(A[7:2]), .WD(WD), .WE(and_6_out), .CLK(CLK), .RD(_64b_mem_2_rd));
  _64B_MEM _64b_mem_3 (.A(A[7:2]), .WD(WD), .WE(and_7_out), .CLK(CLK), .RD(_64b_mem_3_rd));
  _64B_MEM _64b_mem_4 (.A(A[7:2]), .WD(WD), .WE(and_8_out), .CLK(CLK), .RD(_64b_mem_4_rd));
  assign RD = and_1_out ? _64b_mem_1_rd : 8'bz;  // Driver driver_1
  assign RD = and_2_out ? _64b_mem_2_rd : 8'bz;  // Driver driver_2
  assign RD = and_3_out ? _64b_mem_3_rd : 8'bz;  // Driver driver_3
  assign RD = and_4_out ? _64b_mem_4_rd : 8'bz;  // Driver driver_4
endmodule
