// Digital circuit ADD_8.dig as structural Verilog
module ADD_8 (
  input  Cin,
  input  [7:0] A,
  input  [7:0] B,
  output [7:0] S,
  output Cout
);

  CSA_8 csa_8_1 (.Cin(Cin), .A(A), .B(B), .S(S), .Cout(Cout));
endmodule
