// Digital circuit ADD_SUB_8.dig as structural Verilog
module ADD_SUB_8 (
  input  [7:0] A,
  input  [7:0] B,
  input  SUB,
  output [7:0] S,
  output Cout
);

  wire [7:0] ext_1_8_1_o, xor_1_out;

  EXT_1_8 ext_1_8_1 (.I(SUB), .O(ext_1_8_1_o));
  assign xor_1_out = B ^ ext_1_8_1_o;  // XOr xor_1, 8 bits wide
  ADD_8 add_8_1 (.Cin(SUB), .A(A), .B(xor_1_out), .S(S), .Cout(Cout));
endmodule
