// Digital circuit COMPUTER.dig as structural Verilog
module COMPUTER (
  input  CLK,
  input  [15:0] INSTR
);

  wire ctrl_unit_1_op2sel, ctrl_unit_1_rwe;
  wire [2:0] ctrl_unit_1_alop, ctrl_unit_1_rda, ctrl_unit_1_rsa1, ctrl_unit_1_rsa2;
  wire [7:0] _8_register_bank_1_rd1, _8_register_bank_1_rd2, alu_8_1_s, ctrl_unit_1_op2im, multiplexer_1_out;

  CTRL_UNIT ctrl_unit_1 (
    .INSTR(INSTR), .RSA1(ctrl_unit_1_rsa1), .RSA2(ctrl_unit_1_rsa2), .RDA(ctrl_unit_1_rda),
    .RWE(ctrl_unit_1_rwe), .ALOP(ctrl_unit_1_alop), .OP2Sel(ctrl_unit_1_op2sel), .OP2Im(ctrl_unit_1_op2im));  // open: RDSrc, MemWE, PCNext
  _8_REGISTER_BANK _8_register_bank_1 (
    .A1(ctrl_unit_1_rsa1), .A2(ctrl_unit_1_rsa2), .A3(ctrl_unit_1_rda), .WD3(alu_8_1_s),
    .WE3(ctrl_unit_1_rwe), .CLK(CLK), .RD1(_8_register_bank_1_rd1), .RD2(_8_register_bank_1_rd2));
  Multiplexer #(.Bits(8)) multiplexer_1 (
    .sel(ctrl_unit_1_op2sel), .in_0(_8_register_bank_1_rd2), .in_1(ctrl_unit_1_op2im), .out(multiplexer_1_out));
  ALU_8 alu_8_1 (.A(_8_register_bank_1_rd1), .B(multiplexer_1_out), .OP(ctrl_unit_1_alop), .S(alu_8_1_s));
endmodule
