// Digital circuit CRA_8.dig as structural Verilog
module CRA_8 (
  input  Cin,
  input  [7:0] A,
  input  [7:0] B,
  output [7:0] S,
  output Cout
);

  wire fa_1_cout, fa_2_cout, fa_3_cout, fa_4_cout, fa_5_cout, fa_6_cout, fa_7_cout;

  FA fa_1 (.Cin(Cin), .A(A[0]), .B(B[0]), .S(S[0]), .Cout(fa_1_cout));
  FA fa_2 (.Cin(fa_1_cout), .A(A[1]), .B(B[1]), .S(S[1]), .Cout(fa_2_cout));
  FA fa_3 (.Cin(fa_2_cout), .A(A[2]), .B(B[2]), .S(S[2]), .Cout(fa_3_cout));
  FA fa_4 (.Cin(fa_3_cout), .A(A[3]), .B(B[3]), .S(S[3]), .Cout(fa_4_cout));
  FA fa_5 (.Cin(fa_4_cout), .A(A[4]), .B(B[4]), .S(S[4]), .Cout(fa_5_cout));
  FA fa_6 (.Cin(fa_5_cout), .A(A[5]), .B(B[5]), .S(S[5]), .Cout(fa_6_cout));
  FA fa_7 (.Cin(fa_6_cout), .A(A[6]), .B(B[6]), .S(S[6]), .Cout(fa_7_cout));
  FA fa_8 (.Cin(fa_7_cout), .A(A[7]), .B(B[7]), .S(S[7]), .Cout(Cout));
endmodule
