// Digital circuit CSavA_8.dig as structural Verilog
module CSavA_8 (
  input  [7:0] A,
  input  [7:0] B,
  input  [7:0] C,
  output [7:0] S,
  output [7:0] Cout
);

  FA fa_1 (.Cin(A[0]), .A(B[0]), .B(C[0]), .S(S[0]), .Cout(Cout[1]));
  FA fa_2 (.Cin(A[1]), .A(B[1]), .B(C[1]), .S(S[1]), .Cout(Cout[2]));
  FA fa_3 (.Cin(A[2]), .A(B[2]), .B(C[2]), .S(S[2]), .Cout(Cout[3]));
  FA fa_4 (.Cin(A[3]), .A(B[3]), .B(C[3]), .S(S[3]), .Cout(Cout[4]));
  FA fa_5 (.Cin(A[4]), .A(B[4]), .B(C[4]), .S(S[4]), .Cout(Cout[5]));
  FA fa_6 (.Cin(A[5]), .A(B[5]), .B(C[5]), .S(S[5]), .Cout(Cout[6]));
  FA fa_7 (.Cin(A[6]), .A(B[6]), .B(C[6]), .S(S[6]), .Cout(Cout[7]));
  FA fa_8 (.Cin(A[7]), .A(B[7]), .B(C[7]), .S(S[7]));  // open: Cout

  assign Cout[0] = 1'b0;
endmodule
