// Digital circuit CSavA_8_4_2.dig as structural Verilog
module CSavA_8_4_2 (
  input  [7:0] A,
  input  [7:0] B,
  input  [7:0] C,
  input  [7:0] D,
  output [7:0] S0,
  output [7:0] S1
);

  wire [7:0] csava_8_1_cout, csava_8_1_s;

  CSavA_8 csava_8_1 (.A(A), .B(B), .C(C), .S(csava_8_1_s), .Cout(csava_8_1_cout));
  CSavA_8 csava_8_2 (.A(csava_8_1_s), .B(csava_8_1_cout), .C(D), .S(S0), .Cout(S1));
endmodule
