// Digital circuit CTRL_UNIT.dig as structural Verilog
module CTRL_UNIT (
  input  [15:0] INSTR,
  output [2:0] RSA1,
  output [2:0] RSA2,
  output [2:0] RDA,
  output RWE,
  output [7:0] RS2Im,
  output [2:0] ALOP
);

  not not_1 (RWE, INSTR[0]);
  // Not not_2 has open pins: in=INSTR[1], out=open

  assign ALOP = INSTR[6:4];
  assign RDA = INSTR[15:13];
  assign RS2Im = INSTR[12:5];
  assign RSA1 = INSTR[12:10];
  assign RSA2 = INSTR[9:7];

  // Notes on the sheet:
  //   Call / Jump 
  //   / Arithm. Imm.
  //   Branch (S Ext)
  //   Load (Z Ext)
  //   Store (Z Ext)
  //   Load Imm.
  //   ALU Operation
  //   Register Source /
  //   Destination Addresses
  //   Register Destination
  //   Write Enable
  //   Register 2 Immediate
  //   Input
endmodule
