// Digital circuit D_FLIPFLOP.dig as structural Verilog
// D Flip-Flop that stores on the rising edge of the clock (CLK) signal
module D_FLIPFLOP (
  input  D,
  input  CLK,
  output Q,
  output NQ
);

  wire and_1_out, delay_1_out, not_1_out;

  Delay delay_1 (.in(CLK), .out(delay_1_out));
  not not_1 (not_1_out, delay_1_out);
  and and_1 (and_1_out, CLK, not_1_out);
  D_LATCH d_latch_1 (.D(D), .E(and_1_out), .Q(Q), .NQ(NQ));
endmodule
