// Digital circuit 256B_MEM_IO.dig as structural Verilog
module _256B_MEM_IO (
  input  [7:0] A,
  input  [7:0] WD,
  input  WE,
  input  CLK,
  input  [15:0] IN,
  output [7:0] RD,
  output [47:0] OUT
);

  wire and_1_out, and_2_out, and_3_out, demultiplexer_1_out_0, demultiplexer_1_out_1, demultiplexer_1_out_2,
       demultiplexer_1_out_3, demultiplexer_1_out_4, demultiplexer_1_out_5, not_1_out;
  wire [7:0] _256b_mem_1_rd, multiplexer_1_out;

  and and_1 (and_1_out, A[1], A[2], A[3], A[4], A[5], A[6], A[7]);
  and and_2 (and_2_out, A[3], A[4], A[5], A[6], A[7]);
  and and_3 (and_3_out, and_2_out, WE);
  Multiplexer #(.Bits(8)) multiplexer_1 (.sel(A[0]), .in_0(IN[7:0]), .in_1(IN[15:8]), .out(multiplexer_1_out));
  Demultiplexer #(.Selector_Bits(3)) demultiplexer_1 (
    .sel(A[2:0]), .in(and_3_out), .out_0(demultiplexer_1_out_0), .out_1(demultiplexer_1_out_1),
    .out_2(demultiplexer_1_out_2), .out_3(demultiplexer_1_out_3), .out_4(demultiplexer_1_out_4),
    .out_5(demultiplexer_1_out_5));  // open: out_6, out_7
  _256B_MEM _256b_mem_1 (.A(A), .WD(WD), .WE(WE), .CLK(CLK), .RD(_256b_mem_1_rd));
  REGISTER_8 register_8_1 (.D(WD), .E(demultiplexer_1_out_0), .CLK(CLK), .Q(OUT[7:0]));
  REGISTER_8 register_8_2 (.D(WD), .E(demultiplexer_1_out_1), .CLK(CLK), .Q(OUT[15:8]));
  REGISTER_8 register_8_3 (.D(WD), .E(demultiplexer_1_out_2), .CLK(CLK), .Q(OUT[23:16]));
  REGISTER_8 register_8_4 (.D(WD), .E(demultiplexer_1_out_3), .CLK(CLK), .Q(OUT[31:24]));
  REGISTER_8 register_8_5 (.D(WD), .E(demultiplexer_1_out_4), .CLK(CLK), .Q(OUT[39:32]));
  REGISTER_8 register_8_6 (.D(WD), .E(demultiplexer_1_out_5), .CLK(CLK), .Q(OUT[47:40]));
  not not_1 (not_1_out, and_1_out);
  Multiplexer #(.Bits(8)) multiplexer_2 (.sel(not_1_out), .in_0(multiplexer_1_out), .in_1(_256b_mem_1_rd), .out(RD));

  // Notes on the sheet:
  //   Inputs at 255 and 254
  //   (0b1111111x)
  //   Outputs at 248...253
  //   (0b11111xxx)
endmodule
