// Digital circuit 256_INSTR_MEM.dig as structural Verilog
module _256_INSTR_MEM (
  input  [15:0] A,
  input  [15:0] WD,
  input  WE,
  input  CLK,
  output [15:0] RD
);

  // _256B_MEM _256b_mem_1: pin names not known; wires that end beside it: A[7:0], WD, WE, CLK, RD[7:0]
  // _256B_MEM _256b_mem_2: pin names not known; wires that end beside it: A[15:8], WD, WE, CLK, RD[15:8]
  // Pins of 8 and 16 bits meet at A
endmodule
