// Digital circuit 8_REGISTER_BANK.dig as structural Verilog
module _8_REGISTER_BANK (
  input  [2:0] A1,
  input  [2:0] A2,
  input  [2:0] A3,
  input  [7:0] WD3,
  input  WE3,
  input  CLK,
  output [7:0] RD1,
  output [7:0] RD2
);

  wire demultiplexer_1_out_0, demultiplexer_1_out_1, demultiplexer_1_out_2, demultiplexer_1_out_3,
       demultiplexer_1_out_4, demultiplexer_1_out_5, demultiplexer_1_out_6, demultiplexer_1_out_7;
  wire [7:0] register_8_1_q, register_8_2_q, register_8_3_q, register_8_4_q, register_8_5_q, register_8_6_q,
       register_8_7_q, register_8_8_q;

  Demultiplexer #(.Selector_Bits(3)) demultiplexer_1 (
    .sel(A3), .in(WE3), .out_0(demultiplexer_1_out_0), .out_1(demultiplexer_1_out_1),
    .out_2(demultiplexer_1_out_2), .out_3(demultiplexer_1_out_3), .out_4(demultiplexer_1_out_4),
    .out_5(demultiplexer_1_out_5), .out_6(demultiplexer_1_out_6), .out_7(demultiplexer_1_out_7));
  REGISTER_8 register_8_1 (.D(WD3), .E(demultiplexer_1_out_0), .CLK(CLK), .Q(register_8_1_q));
  REGISTER_8 register_8_2 (.D(WD3), .E(demultiplexer_1_out_1), .CLK(CLK), .Q(register_8_2_q));
  REGISTER_8 register_8_3 (.D(WD3), .E(demultiplexer_1_out_2), .CLK(CLK), .Q(register_8_3_q));
  REGISTER_8 register_8_4 (.D(WD3), .E(demultiplexer_1_out_3), .CLK(CLK), .Q(register_8_4_q));
  REGISTER_8 register_8_5 (.D(WD3), .E(demultiplexer_1_out_4), .CLK(CLK), .Q(register_8_5_q));
  REGISTER_8 register_8_6 (.D(WD3), .E(demultiplexer_1_out_5), .CLK(CLK), .Q(register_8_6_q));
  REGISTER_8 register_8_7 (.D(WD3), .E(demultiplexer_1_out_6), .CLK(CLK), .Q(register_8_7_q));
  REGISTER_8 register_8_8 (.D(WD3), .E(demultiplexer_1_out_7), .CLK(CLK), .Q(register_8_8_q));
  Multiplexer #(.Selector_Bits(3), .Bits(8)) multiplexer_1 (
    .sel(A1), .in_0(register_8_1_q), .in_1(register_8_2_q), .in_2(register_8_3_q), .in_3(register_8_4_q),
    .in_4(register_8_5_q), .in_5(register_8_6_q), .in_6(register_8_7_q), .in_7(register_8_8_q), .out(RD1));
  Multiplexer #(.Selector_Bits(3), .Bits(8)) multiplexer_2 (
    .sel(A2), .in_0(register_8_1_q), .in_1(register_8_2_q), .in_2(register_8_3_q), .in_3(register_8_4_q),
    .in_4(register_8_5_q), .in_5(register_8_6_q), .in_6(register_8_7_q), .in_7(register_8_8_q), .out(RD2));
endmodule
