// Digital circuit ALU_8.dig as structural Verilog
module ALU_8 (
  input  [7:0] A,
  input  [7:0] B,
  input  [2:0] OP,
  output [7:0] S,
  output Z,
  output C
);

  wire [7:0] add_8_1_s, and_1_out, mul_8_1_s, or_1_out, sll_8_1_o, srl_8_1_o, sub_8_1_s, xor_1_out;

  ADD_8 add_8_1 (.Cin(1'b0), .A(A), .B(B), .S(add_8_1_s));  // open: Cout
  SUB_8 sub_8_1 (.A(A), .B(B), .S(sub_8_1_s), .Cout(C));
  MUL_8 mul_8_1 (.A(A), .B(B), .S(mul_8_1_s));
  SLL_8 sll_8_1 (.A(A), .S(B[2:0]), .O(sll_8_1_o));
  SRL_8 srl_8_1 (.A(A), .S(B[2:0]), .O(srl_8_1_o));
  assign and_1_out = A & B;  // And and_1, 8 bits wide
  assign or_1_out = A | B;  // Or or_1, 8 bits wide
  assign xor_1_out = A ^ B;  // XOr xor_1, 8 bits wide
  Multiplexer #(.Selector_Bits(3), .Bits(8)) multiplexer_1 (
    .sel(OP), .in_0(add_8_1_s), .in_1(sub_8_1_s), .in_2(mul_8_1_s), .in_3(sll_8_1_o), .in_4(srl_8_1_o),
    .in_5(and_1_out), .in_6(or_1_out), .in_7(xor_1_out), .out(S));
  // IS_ZERO_8 is_zero_8_1: pin names not known; wires that end beside it: sub_8_1_s, Z

  // Notes on the sheet:
  //   Comparison signals 
  //   obtained from SUB
endmodule
