// Digital circuit CMPU_8.dig as structural Verilog
module CMPU_8 (
  input  [7:0] A,
  input  [7:0] B,
  output LT,
  output EQ,
  output GT
);

  wire sub_8_1_cout;
  wire [7:0] sub_8_1_s;

  SUB_8 sub_8_1 (.A(A), .B(B), .S(sub_8_1_s), .Cout(sub_8_1_cout));
  nor nor_1 (EQ, sub_8_1_s[7], sub_8_1_s[6], sub_8_1_s[5], sub_8_1_s[4], sub_8_1_s[3], sub_8_1_s[2], sub_8_1_s[1], sub_8_1_s[0]);
  not not_1 (LT, sub_8_1_cout);
  and and_1 (GT, sub_8_1_cout, ~EQ);  // And
endmodule
