// Digital circuit CMPU_CTRL.dig as structural Verilog
module CMPU_CTRL (
  input  [1:0] OP,
  input  Z,
  input  C,
  output Q
);

  wire and_1_out, not_1_out, not_2_out;

  not not_1 (not_1_out, Z);
  not not_2 (not_2_out, C);
  and and_1 (and_1_out, C, ~Z);  // And
  Multiplexer #(.Selector_Bits(2)) multiplexer_1 (
    .sel(OP), .in_0(Z), .in_1(not_1_out), .in_2(not_2_out), .in_3(and_1_out), .out(Q));

  // Notes on the sheet:
  //   EQ
  //   NEQ
  //   LT
  //   GE
endmodule
