// Digital circuit COUNTER_8.dig as structural Verilog
module COUNTER_8 (
  input  E,
  input  R,
  input  CLK,
  output [7:0] Q
);

  wire and_1_out, and_2_out, and_3_out, and_4_out, and_5_out, and_6_out, and_7_out;

  T_FF t_ff_1 (.T(E), .R(R), .CLK(CLK), .Q(Q[0]));  // open: NQ
  and and_1 (and_1_out, E, Q[0]);
  T_FF t_ff_2 (.T(and_1_out), .R(R), .CLK(CLK), .Q(Q[1]));  // open: NQ
  and and_2 (and_2_out, and_1_out, Q[1]);
  T_FF t_ff_3 (.T(and_2_out), .R(R), .CLK(CLK), .Q(Q[2]));  // open: NQ
  and and_3 (and_3_out, and_2_out, Q[2]);
  T_FF t_ff_4 (.T(and_3_out), .R(R), .CLK(CLK), .Q(Q[3]));  // open: NQ
  and and_4 (and_4_out, and_3_out, Q[3]);
  T_FF t_ff_5 (.T(and_4_out), .R(R), .CLK(CLK), .Q(Q[4]));  // open: NQ
  and and_5 (and_5_out, and_4_out, Q[4]);
  T_FF t_ff_6 (.T(and_5_out), .R(R), .CLK(CLK), .Q(Q[5]));  // open: NQ
  and and_6 (and_6_out, and_5_out, Q[5]);
  T_FF t_ff_7 (.T(and_6_out), .R(R), .CLK(CLK), .Q(Q[6]));  // open: NQ
  and and_7 (and_7_out, and_6_out, Q[6]);
  T_FF t_ff_8 (.T(and_7_out), .R(R), .CLK(CLK), .Q(Q[7]));  // open: NQ
endmodule
