// Digital circuit CSA_2.dig as structural Verilog
module CSA_2 (
  input  Cin,
  input  [1:0] A,
  input  [1:0] B,
  output [1:0] S,
  output Cout
);

  wire fa_1_cout, fa_2_cout, fa_2_s, fa_3_cout, fa_3_s;

  FA fa_1 (.Cin(Cin), .A(A[0]), .B(B[0]), .S(S[0]), .Cout(fa_1_cout));
  FA fa_2 (.Cin(1'b0), .A(A[1]), .B(B[1]), .S(fa_2_s), .Cout(fa_2_cout));
  FA fa_3 (.Cin(1'b1), .A(A[1]), .B(B[1]), .S(fa_3_s), .Cout(fa_3_cout));
  Multiplexer multiplexer_1 (.sel(fa_1_cout), .in_0(fa_2_s), .in_1(fa_3_s), .out(S[1]));
  Multiplexer multiplexer_2 (.sel(fa_1_cout), .in_0(fa_2_cout), .in_1(fa_3_cout), .out(Cout));
endmodule
