// Digital circuit CSA_4.dig as structural Verilog
module CSA_4 (
  input  Cin,
  input  [3:0] A,
  input  [3:0] B,
  output [3:0] S,
  output Cout
);

  wire csa_2_1_cout, csa_2_2_cout, csa_2_3_cout;
  wire [1:0] csa_2_2_s, csa_2_3_s;

  CSA_2 csa_2_1 (.Cin(Cin), .A(A[1:0]), .B(B[1:0]), .S(S[1:0]), .Cout(csa_2_1_cout));
  CSA_2 csa_2_2 (.Cin(1'b0), .A(A[3:2]), .B(B[3:2]), .S(csa_2_2_s), .Cout(csa_2_2_cout));
  CSA_2 csa_2_3 (.Cin(1'b1), .A(A[3:2]), .B(B[3:2]), .S(csa_2_3_s), .Cout(csa_2_3_cout));
  Multiplexer #(.Bits(2)) multiplexer_1 (.sel(csa_2_1_cout), .in_0(csa_2_2_s), .in_1(csa_2_3_s), .out(S[3:2]));
  Multiplexer multiplexer_2 (.sel(csa_2_1_cout), .in_0(csa_2_2_cout), .in_1(csa_2_3_cout), .out(Cout));
endmodule
