// Digital circuit CSA_8.dig as structural Verilog
module CSA_8 (
  input  Cin,
  input  [7:0] A,
  input  [7:0] B,
  output [7:0] S,
  output Cout
);

  wire csa_4_1_cout, csa_4_2_cout, csa_4_3_cout;
  wire [3:0] csa_4_2_s, csa_4_3_s;

  CSA_4 csa_4_1 (.Cin(Cin), .A(A[3:0]), .B(B[3:0]), .S(S[3:0]), .Cout(csa_4_1_cout));
  CSA_4 csa_4_2 (.Cin(1'b0), .A(A[7:4]), .B(B[7:4]), .S(csa_4_2_s), .Cout(csa_4_2_cout));
  CSA_4 csa_4_3 (.Cin(1'b1), .A(A[7:4]), .B(B[7:4]), .S(csa_4_3_s), .Cout(csa_4_3_cout));
  Multiplexer #(.Bits(4)) multiplexer_1 (.sel(csa_4_1_cout), .in_0(csa_4_2_s), .in_1(csa_4_3_s), .out(S[7:4]));
  Multiplexer multiplexer_2 (.sel(csa_4_1_cout), .in_0(csa_4_2_cout), .in_1(csa_4_3_cout), .out(Cout));
endmodule
