// Digital circuit D_LATCH.dig as structural Verilog
module D_LATCH (
  input  D,
  input  E,
  output Q,
  output NQ
);

  wire and_1_out, and_2_out;

  and and_1 (and_1_out, D, E);
  and and_2 (and_2_out, ~D, E);  // And
  SR_LATCH sr_latch_1 (.S(and_1_out), .R(and_2_out), .Q(Q), .NQ(NQ));
endmodule
