// Digital circuit FA.dig as structural Verilog
module FA (
  input  Cin,
  input  A,
  input  B,
  output S,
  output Cout
);

  wire ha_1_c, ha_1_s, ha_2_c;

  HA ha_1 (.A(Cin), .B(A), .S(ha_1_s), .C(ha_1_c));
  HA ha_2 (.A(ha_1_s), .B(B), .S(S), .C(ha_2_c));
  or or_1 (Cout, ha_2_c, ha_1_c);
endmodule
