// Digital circuit GATE_8.dig as structural Verilog
module GATE_8 (
  input  E,
  input  [7:0] D,
  output [7:0] Q
);

  wire multiplexer_1_out;

  Multiplexer multiplexer_1 (.sel(E), .in_0(1'b0), .in_1(1'b1), .out(multiplexer_1_out));
  and and_1 (Q[0], D[0], multiplexer_1_out);
  // Pins of 1 and 8 bits meet at Q
  // Pins of 1 and 8 bits meet at D
  // Pins of 1 and 8 bits meet at {8{1'b0}}
  // Pins of 1 and 8 bits meet at {8{1'b1}}
endmodule
