// Digital circuit IS_EQU_8.dig as structural Verilog
module IS_EQU_8 (
  input  [7:0] A,
  input  [7:0] B,
  output EQ
);

  wire [7:0] xor_1_out;

  assign xor_1_out = A ^ B;  // XOr xor_1, 8 bits wide
  nor nor_1 (EQ, xor_1_out[0], xor_1_out[1], xor_1_out[2], xor_1_out[3], xor_1_out[4], xor_1_out[5], xor_1_out[6], xor_1_out[7]);
endmodule
