// Digital circuit REGISTER_1.dig as structural Verilog
module REGISTER_1 (
  input  D,
  input  E,
  input  CLK,
  output Q
);

  wire and_1_out, and_2_out, or_1_out;

  and and_1 (and_1_out, Q, ~E);  // And
  and and_2 (and_2_out, E, D);
  or or_1 (or_1_out, and_1_out, and_2_out);
  D_FLIPFLOP d_flipflop_1 (.D(or_1_out), .CLK(CLK), .Q(Q));  // open: NQ
endmodule
