// Digital circuit REGISTER_8.dig as structural Verilog
module REGISTER_8 (
  input  [7:0] D,
  input  E,
  input  CLK,
  output [7:0] Q
);

  REGISTER_1 register_1_1 (.D(D[0]), .E(E), .CLK(CLK), .Q(Q[0]));
  REGISTER_1 register_1_2 (.D(D[1]), .E(E), .CLK(CLK), .Q(Q[1]));
  REGISTER_1 register_1_3 (.D(D[2]), .E(E), .CLK(CLK), .Q(Q[2]));
  REGISTER_1 register_1_4 (.D(D[3]), .E(E), .CLK(CLK), .Q(Q[3]));
  REGISTER_1 register_1_5 (.D(D[4]), .E(E), .CLK(CLK), .Q(Q[4]));
  REGISTER_1 register_1_6 (.D(D[5]), .E(E), .CLK(CLK), .Q(Q[5]));
  REGISTER_1 register_1_7 (.D(D[6]), .E(E), .CLK(CLK), .Q(Q[6]));
  REGISTER_1 register_1_8 (.D(D[7]), .E(E), .CLK(CLK), .Q(Q[7]));
endmodule
