// Digital circuit SRL_8.dig as structural Verilog
module SRL_8 (
  input  [7:0] A,
  input  [2:0] S,
  output [7:0] O
);

  wire [7:0] multiplexer_1_out, multiplexer_2_out;

  Multiplexer #(.Bits(8)) multiplexer_1 (.sel(S[0]), .in_0(A), .in_1({1'b0, A[7:1]}), .out(multiplexer_1_out));
  Multiplexer #(.Bits(8)) multiplexer_2 (
    .sel(S[1]), .in_0(multiplexer_1_out), .in_1({2'b00, multiplexer_1_out[7:2]}), .out(multiplexer_2_out));
  Multiplexer #(.Bits(8)) multiplexer_3 (
    .sel(S[2]), .in_0(multiplexer_2_out), .in_1({4'b0000, multiplexer_2_out[7:4]}), .out(O));
endmodule
