// Digital circuit T_FF.dig as structural Verilog
module T_FF (
  input  T,
  input  R,
  input  CLK,
  output Q,
  output NQ
);

  wire and_1_out, and_2_out, or_1_out;

  and and_1 (and_1_out, Q, ~T, ~R);  // And
  and and_2 (and_2_out, T, ~R, NQ);  // And
  or or_1 (or_1_out, and_1_out, and_2_out);
  D_FLIPFLOP d_flipflop_1 (.D(or_1_out), .CLK(CLK), .Q(Q), .NQ(NQ));
endmodule
