// Digital circuit MUL_8.dig as structural Verilog
module MUL_8 (
  input  [7:0] A,
  input  [7:0] B,
  output [7:0] S
);

  wire [7:0] and_1_out, and_2_out, and_3_out, and_4_out, and_5_out, and_6_out, and_7_out, and_8_out,
       csava_8_4_2_1_s0, csava_8_4_2_1_s1, csava_8_4_2_2_s0, csava_8_4_2_2_s1, csava_8_4_2_3_s0,
       csava_8_4_2_3_s1, ext_1_8_1_o, ext_1_8_2_o, ext_1_8_3_o, ext_1_8_4_o, ext_1_8_5_o, ext_1_8_6_o,
       ext_1_8_7_o, ext_1_8_8_o;

  EXT_1_8 ext_1_8_1 (.I(A[0]), .O(ext_1_8_1_o));
  EXT_1_8 ext_1_8_2 (.I(A[1]), .O(ext_1_8_2_o));
  EXT_1_8 ext_1_8_3 (.I(A[2]), .O(ext_1_8_3_o));
  EXT_1_8 ext_1_8_4 (.I(A[3]), .O(ext_1_8_4_o));
  EXT_1_8 ext_1_8_5 (.I(A[4]), .O(ext_1_8_5_o));
  EXT_1_8 ext_1_8_6 (.I(A[5]), .O(ext_1_8_6_o));
  EXT_1_8 ext_1_8_7 (.I(A[6]), .O(ext_1_8_7_o));
  EXT_1_8 ext_1_8_8 (.I(A[7]), .O(ext_1_8_8_o));
  assign and_1_out = ext_1_8_1_o & B;  // And and_1, 8 bits wide
  assign and_2_out = ext_1_8_2_o & {B[6:0], 1'b0};  // And and_2, 8 bits wide
  assign and_3_out = ext_1_8_3_o & {B[5:0], 2'b00};  // And and_3, 8 bits wide
  assign and_4_out = ext_1_8_4_o & {B[4:0], 3'b000};  // And and_4, 8 bits wide
  assign and_5_out = ext_1_8_5_o & {B[3:0], 4'b0000};  // And and_5, 8 bits wide
  assign and_6_out = ext_1_8_6_o & {B[2:0], {5{1'b0}}};  // And and_6, 8 bits wide
  assign and_7_out = ext_1_8_7_o & {B[1:0], {6{1'b0}}};  // And and_7, 8 bits wide
  assign and_8_out = ext_1_8_8_o & {B[0], {7{1'b0}}};  // And and_8, 8 bits wide
  CSavA_8_4_2 csava_8_4_2_1 (
    .A(and_1_out), .B(and_2_out), .C(and_3_out), .D(and_4_out), .S0(csava_8_4_2_1_s0), .S1(csava_8_4_2_1_s1));
  CSavA_8_4_2 csava_8_4_2_2 (
    .A(and_5_out), .B(and_6_out), .C(and_7_out), .D(and_8_out), .S0(csava_8_4_2_2_s0), .S1(csava_8_4_2_2_s1));
  CSavA_8_4_2 csava_8_4_2_3 (
    .A(csava_8_4_2_1_s0), .B(csava_8_4_2_1_s1), .C(csava_8_4_2_2_s0), .D(csava_8_4_2_2_s1),
    .S0(csava_8_4_2_3_s0), .S1(csava_8_4_2_3_s1));
  ADD_8 add_8_1 (.Cin(1'b0), .A(csava_8_4_2_3_s0), .B(csava_8_4_2_3_s1), .S(S));  // open: Cout
endmodule
