// Digital circuit SLL_8.dig as structural Verilog
module SLL_8 (
  input  [7:0] A,
  input  [2:0] S,
  output [7:0] O
);

  wire [7:0] multiplexer_1_out;
  wire [7:4] multiplexer_2_out, multiplexer_2_out_2;

  Multiplexer #(.Bits(8)) multiplexer_1 (.sel(S[0]), .in_0(A), .in_1({A[6:0], 1'b0}), .out(multiplexer_1_out));
  Multiplexer #(.Bits(8)) multiplexer_2 (
    .sel(S[1]), .in_0(multiplexer_1_out), .in_1({multiplexer_1_out[5:0], 2'b00}),
    .out({multiplexer_2_out_2, multiplexer_2_out}));
  Multiplexer #(.Bits(8)) multiplexer_3 (
    .sel(S[2]), .in_0({multiplexer_2_out_2, multiplexer_2_out}), .in_1({multiplexer_2_out, 4'b0000}), .out(O));
endmodule
