// Digital circuit SRA_8.dig as structural Verilog
module SRA_8 (
  input  [7:0] A,
  input  [2:0] S,
  output [7:0] O
);

  wire [1:0] multiplexer_1_out;
  wire [7:0] multiplexer_1_out_2, multiplexer_2_out;

  Multiplexer #(.Bits(8)) multiplexer_1 (
    .sel(S[0]), .in_0(A), .in_1({{2{A[7]}}, A[6:1]}),
    .out({multiplexer_1_out_2[7], multiplexer_1_out_2[4:0], multiplexer_1_out}));
  Multiplexer #(.Bits(8)) multiplexer_2 (
    .sel(S[1]), .in_0({multiplexer_1_out_2[7], multiplexer_1_out_2[4:0], multiplexer_1_out}),
    .in_1({{3{multiplexer_1_out_2[7]}}, multiplexer_1_out_2[4:0]}), .out(multiplexer_2_out));
  Multiplexer #(.Bits(8)) multiplexer_3 (
    .sel(S[2]), .in_0(multiplexer_2_out), .in_1({{5{multiplexer_2_out[7]}}, multiplexer_2_out[6:4]}), .out(O));
endmodule
