// Digital circuit SUB_8.dig as structural Verilog
module SUB_8 (
  input  [7:0] A,
  input  [7:0] B,
  output [7:0] S,
  output Cout
);

  wire [7:0] not_1_out;

  assign not_1_out = ~B;  // Not not_1, 8 bits wide
  ADD_8 add_8_1 (.Cin(1'b1), .A(A), .B(not_1_out), .S(S), .Cout(Cout));
endmodule
